# Fritzing sketch Timer (saved by Fritzing 0.9.3b)
breadboards: 1

parts:
  Componente1 = Arduino Uno (Rev3)
  Grove1 = Grove OLED 128x96
  S1 = Pushbutton [package="[THT]"]
  S2 = Pushbutton [package="[THT]"]
  R1 = Resistor [tolerance=±5% resistance=220 package=THT]
  R2 = Resistor [tolerance=±5% resistance=220 package=THT]
  KY-1 = Keyes Relay [package=THT]

nets:
  N1: Componente1.A0, S1.Pin_1, S1.Pin_2, R2.Pin_1
  N2: Componente1.A1, S2.Pin_1, S2.Pin_2, R1.Pin_1
  N3: Componente1.D8, KY-1.signal
  N4: Componente1.A4/SDA, Grove1.SDA
  N5: Componente1.A5/SCL, Grove1.SCL
  N6: Grove1.GND, R1.Pin_0, R2.Pin_0, KY-1.ground
  N7: Grove1.VCC, S1.Pin_3, S1.Pin_4, S2.Pin_3, S2.Pin_4, KY-1.power

custom parts:
  Keyes Relay: The Keyes 5V relay module is suitable for SCM development, home appliance control. It uses a 5V~12V TIL control signal which can control DC / AC signal.
